// Logisim project alu.circ as structural Verilog: 17 circuits, main circuit main
module main (
  input  [15:0] X,
  input  [15:0] Y,
  input  [3:0] switch__S,
  output signed_overflow,
  output [15:0] result,
  output equal
);

  wire add_1_out, and_2_out, and_3_out, signoverflow2_1_out, signoverflow_1_out, sub_1_out;
  wire [15:0] add_1_output, and_1_out, bc_1_out_3, ffo_1_out_3, lui_1_out_3, or_1_out, sllv_1_out, slt_1_out,
       srav_1_out, srlv_1_out, sub_1_output, zb_1_out_3;

  \and  and_1 (.X(X), .Y(Y), .out(and_1_out));
  \or  or_1 (.X(X), .Y(Y), .out(or_1_out));
  slt slt_1 (.X(X), .Y(Y), .out(slt_1_out));
  sllv sllv_1 (.X(X), .y(Y), .out(sllv_1_out));
  srlv srlv_1 (.X(X), .y(Y), .out(srlv_1_out));
  srav srav_1 (.X(X), .y(Y), .out(srav_1_out));
  Add add_1 (.X(X), .Y(Y), .\output (add_1_output), .out(add_1_out));
  sub sub_1 (.X(X), .Y(Y), .\output (sub_1_output), .out(sub_1_out));
  lui lui_1 (.X(X), .Y(Y), .out_3(lui_1_out_3));
  ffo ffo_1 (.X(X), .Y(Y), .out_3(ffo_1_out_3));
  zb zb_1 (.X(X), .Y(Y), .out_3(zb_1_out_3));
  bc bc_1 (.X(X), .Y(Y), .out_3(bc_1_out_3));
  Multiplexer #(.select(4), .width(16)) multiplexer_1 (
    .in0(and_1_out), .in1(or_1_out), .in2(slt_1_out), .in3(sllv_1_out), .in4(srlv_1_out), .in5(srav_1_out),
    .in6(add_1_output), .in7(sub_1_output), .in8(lui_1_out_3), .in9(ffo_1_out_3), .in10(zb_1_out_3),
    .in11(bc_1_out_3), .in12({16{1'b0}}), .out(result), .sel(switch__S));  // open: in13, in14, in15, en
  signoverflow signoverflow_1 (.x(switch__S[2]), .y(switch__S[1]), .z(switch__S[0]), .out(signoverflow_1_out));
  signoverflow2 signoverflow2_1 (.x(switch__S[2]), .y(switch__S[1]), .z(switch__S[0]), .out(signoverflow2_1_out));
  Comparator #(.width(16)) comparator_1 (.a(X), .b(Y), .eq(equal));  // open: gt, lt
  and and_2 (and_2_out, signoverflow_1_out, sub_1_out);
  and and_3 (and_3_out, signoverflow2_1_out, add_1_out);
  or or_2 (signed_overflow, and_2_out, and_3_out);

  // Notes on the sheet:
  //   These are INPUTS to your circuit
  //   This is an INPUT to your circuit
  //   DO NOT CHANGE THE LOCATIONS OF THE INPUTS/OUTPUTS! IF YOU DO SO, YOU NEED TO MAKE SURE THE PINS ARE AT THE RIGHT PLACE!
  //   These are OUTPUTS to your circuit
endmodule

// add
module Add (
  input  [15:0] X,
  input  [15:0] Y,
  output [15:0] \output ,
  output out
);

  Adder #(.width(16)) adder_1 (.a(X), .b(Y), .out(\output ));  // open: cin, cout
  addhelp addhelp_1 (.x(X[15]), .y(Y[15]), .out(\output [15]), .\output (out));
endmodule

module \or  (
  input  [15:0] X,
  input  [15:0] Y,
  output [15:0] out
);

  assign out = X | Y;  // OR_Gate or_1, 16 bits wide

  // Notes on the sheet:
  //   OR
endmodule

module \and  (
  input  [15:0] X,
  input  [15:0] Y,
  output [15:0] out
);

  assign out = X & Y;  // AND_Gate and_1, 16 bits wide

  // Notes on the sheet:
  //   AND
endmodule

module slt (
  input  [15:0] X,
  input  [15:0] Y,
  output [15:0] out
);

  wire comparator_1_lt;

  Comparator #(.width(16)) comparator_1 (.a(X), .b(Y), .lt(comparator_1_lt));  // open: gt, eq
  assign out = {{15{1'b0}}, comparator_1_lt};  // Bit_Extender bit_extender_1
endmodule

module sllv (
  input  [15:0] X,
  input  [15:0] y,
  output [15:0] out
);

  Shifter #(.width(16)) shifter_1 (.in(X), .\dist (y[3:0]), .out(out));
endmodule

module srlv (
  input  [15:0] X,
  input  [15:0] y,
  output [15:0] out
);

  Shifter #(.width(16), .shift("lr")) shifter_1 (.in(X), .\dist (y[3:0]), .out(out));
endmodule

module srav (
  input  [15:0] X,
  input  [15:0] y,
  output [15:0] out
);

  Shifter #(.width(16), .shift("ar")) shifter_1 (.in(X), .\dist (y[3:0]), .out(out));
endmodule

module sub (
  input  [15:0] X,
  input  [15:0] Y,
  output [15:0] \output ,
  output out
);

  Subtractor #(.width(16)) subtractor_1 (.a(X), .b(Y), .out(\output ));  // open: bin, bout
  subhelp subhelp_1 (.x(X[15]), .y(Y[15]), .out(\output [15]), .out_2(out));
endmodule

module addhelp (
  input  x,
  input  y,
  input  out,
  output \output 
);

  wire and_1_out, and_2_out, not_1_out, not_2_out, not_3_out;

  not not_1 (not_1_out, x);
  not not_2 (not_2_out, y);
  not not_3 (not_3_out, out);
  and and_1 (and_1_out, x, y, not_3_out);
  and and_2 (and_2_out, not_1_out, not_2_out, out);
  or or_1 (\output , and_1_out, and_2_out);
endmodule

// for7
module signoverflow (
  input  x,
  input  y,
  input  z,
  output out
);

  and and_1 (out, x, z, y);
endmodule

module subhelp (
  input  x,
  input  y,
  input  out,
  output out_2
);

  wire and_1_out, and_2_out, not_1_out, not_2_out, not_3_out;

  not not_1 (not_1_out, x);
  not not_2 (not_2_out, y);
  not not_3 (not_3_out, out);
  and and_1 (and_1_out, not_1_out, y, out);
  and and_2 (and_2_out, x, not_2_out, not_3_out);
  or or_1 (out_2, and_1_out, and_2_out);
endmodule

// for6
module signoverflow2 (
  input  x,
  input  y,
  input  z,
  output out
);

  wire not_1_out;

  not not_1 (not_1_out, z);
  and and_1 (out, x, not_1_out, y);
endmodule

module lui (
  input  [15:0] X,
  input  [15:0] Y,
  output [15:0] out_3
);

  Shifter #(.width(16)) shifter_1 (.in(Y), .\dist (4'b1000), .out(out_3));
endmodule

module ffo (
  input  [15:0] X,
  input  [15:0] Y,
  output [15:0] out_3
);

  wire [3:0] bitfinder_1_index;
  wire [15:0] bit_extender_1_out;

  BitFinder #(.width(16), .\type ("high1")) bitfinder_1 (.in(X), .index(bitfinder_1_index));  // open: found
  assign bit_extender_1_out = {{12{1'b0}}, bitfinder_1_index};  // Bit_Extender bit_extender_1
  Subtractor #(.width(16)) subtractor_1 (.a(16'hf), .b(bit_extender_1_out), .out(out_3));  // open: bin, bout
endmodule

module zb (
  input  [15:0] X,
  input  [15:0] Y,
  output [15:0] out_3
);

  wire comparator_1_eq, comparator_2_eq, or_1_out;

  Comparator comparator_1 (.a(X[7:0]), .b({8{1'b0}}), .eq(comparator_1_eq));  // open: gt, lt
  Comparator comparator_2 (.a({8{1'b0}}), .b(X[15:8]), .eq(comparator_2_eq));  // open: gt, lt
  assign out_3 = {{15{1'b0}}, or_1_out};  // Bit_Extender bit_extender_1
  or or_1 (or_1_out, comparator_1_eq, comparator_2_eq);
endmodule

module bc (
  input  [15:0] X,
  input  [15:0] Y,
  output [15:0] out_3
);

  wire [4:0] bitadder_1_out;

  BitAdder #(.width(16)) bitadder_1 (.in0(X), .out(bitadder_1_out));
  assign out_3 = {{11{1'b0}}, bitadder_1_out};  // Bit_Extender bit_extender_1
endmodule
