// Logisim project cpu.circ as structural Verilog: 3 circuits, main circuit ALU2
module main (
  input  [15:0] From_Instr_Mem,
  input  clk,
  output [15:0] r0,
  output [15:0] r1,
  output [15:0] r2,
  output [15:0] r3,
  output [15:0] Display_0,
  output [15:0] Display_1,
  output [15:0] To_Instr_Mem,
  output [15:0] Data_Mem_Data,
  output [15:0] Data_Mem_Addr,
  output Data_Mem_Write
);

  wire ALUSrc, and_2_out, and_3_out, and_4_out, beq, bne, branch, button_1_out, comparator_1_lt,
       demultiplexer_2_out0, demultiplexer_2_out1, disp, j, jal, jr, main_2_equal, main_2_signed_overflow,
       MemtoReg, nop, not_1_out, not_2_out, or_1_out, RegDst, RegWrite, sign_extend;
  wire [1:0] multiplexer_5_out, multiplexer_6_out;
  wire [3:0] alu2_1_alu_control_input, ALUOp, Control;
  wire [11:0] register_2_q;
  wire [15:0] adder_1_out, adder_2_out, and_1_out, bit_extender_1_out, bit_extender_2_out, DataIn,
       demultiplexer_1_out0, demultiplexer_1_out1, demultiplexer_3_out1, multiplexer_1_out,
       multiplexer_2_out, multiplexer_3_out, multiplexer_4_out, multiplexer_7_out, multiplexer_8_out,
       multiplexer_9_out, multiplexer_10_out, or_2_out, rs;

  Register #(.width(16)) register_1 (.D(multiplexer_1_out), .Q(To_Instr_Mem), .clk(clk));  // open: en, clr
  Adder #(.width(16)) adder_1 (.a(16'h1), .b(To_Instr_Mem), .out(adder_1_out));  // open: cin, cout
  Multiplexer #(.width(16)) multiplexer_1 (
    .in0(multiplexer_4_out), .in1(rs), .out(multiplexer_1_out), .sel(jr));  // open: en
  Adder #(.width(16)) adder_2 (.a(To_Instr_Mem), .b(multiplexer_8_out), .out(adder_2_out));  // open: cin, cout
  Multiplexer #(.width(16)) multiplexer_2 (
    .in0(From_Instr_Mem), .in1({16{1'b0}}), .out(multiplexer_2_out), .sel(nop));  // open: en
  Multiplexer #(.width(16)) multiplexer_3 (
    .in0(adder_1_out), .in1(adder_2_out), .out(multiplexer_3_out), .sel(branch));  // open: en
  Register #(.width(16)) register_2 (.D(multiplexer_2_out), .Q({Control, register_2_q}), .clk(clk));  // open: en, clr
  assign and_1_out = To_Instr_Mem & 16'hf000;  // AND_Gate and_1, 16 bits wide
  Multiplexer #(.width(16)) multiplexer_4 (
    .in0(multiplexer_3_out), .in1(or_2_out), .out(multiplexer_4_out), .sel(or_1_out));  // open: en
  or or_1 (or_1_out, j, jal);
  assign or_2_out = and_1_out | {4'b0000, register_2_q};  // OR_Gate or_2, 16 bits wide
  Multiplexer #(.width(2)) multiplexer_5 (
    .in0(register_2_q[9:8]), .in1(register_2_q[7:6]), .out(multiplexer_5_out), .sel(RegDst));  // open: en
  RAM #(.addrWidth(16), .dataWidth(16)) ram_1 (
    .addr(Data_Mem_Addr), .data(Data_Mem_Data), .sel(1'b1), .clk(clk), .ld(not_1_out), .clr(button_1_out));
  Button button_1 (.out(button_1_out));
  not not_1 (not_1_out, Data_Mem_Write);
  Multiplexer #(.width(2)) multiplexer_6 (
    .in0(multiplexer_5_out), .in1(2'b11), .out(multiplexer_6_out), .sel(jal));  // open: en
  assign Data_Mem_Data = Data_Mem_Write ? DataIn : 16'bz;  // Controlled_Buffer controlled_buffer_1
  assign bit_extender_1_out = {{8{1'b0}}, register_2_q[7:0]};  // Bit_Extender bit_extender_1
  assign bit_extender_2_out = {{8{register_2_q[7]}}, register_2_q[7:0]};  // Bit_Extender bit_extender_2
  Multiplexer #(.width(16)) multiplexer_7 (
    .in0(multiplexer_10_out), .in1(To_Instr_Mem), .out(multiplexer_7_out), .sel(jal));  // open: en
  Multiplexer #(.width(16)) multiplexer_8 (
    .in0(bit_extender_1_out), .in1(bit_extender_2_out), .out(multiplexer_8_out), .sel(sign_extend));  // open: en
  Regfile_main main_1 (
    .Read_register_1(register_2_q[11:10]), .Read_register_2(register_2_q[9:8]),
    .write_register(multiplexer_6_out), .write_data(multiplexer_7_out), .Reg_0_Value(r0), .Reg_1_Value(r1),
    .Reg_2_Value(r2), .Reg_3_Value(r3), .RegWrite(RegWrite), .clock(clk), .Read_Data_1(rs),
    .Read_Data_2(DataIn));
  Multiplexer #(.width(16)) multiplexer_9 (
    .in0(DataIn), .in1(multiplexer_8_out), .out(multiplexer_9_out), .sel(ALUSrc));  // open: en
  not not_2 (not_2_out, main_2_equal);
  alu_main main_2 (
    .switch__S(alu2_1_alu_control_input), .X(rs), .equal(main_2_equal), .result(Data_Mem_Addr),
    .signed_overflow(main_2_signed_overflow), .Y(multiplexer_9_out));
  ALU2 alu2_1 (.funct(register_2_q[5:0]), .ALUOp(ALUOp), .ALU_control_input(alu2_1_alu_control_input));
  and and_2 (and_2_out, beq, main_2_equal);
  or or_3 (branch, and_2_out, and_3_out);
  and and_3 (and_3_out, not_2_out, bne);
  LED signed_overflow (.in(main_2_signed_overflow));
  control control_1 (
    .Con(Control), .ALUOp(ALUOp), .Registerd(RegDst), .RegWrite(RegWrite), .jal(jal), .j(j), .jr(jr),
    .beq(beq), .bne(bne), .MemoryWrite(Data_Mem_Write), .MemorytoRegister(MemtoReg), .disp(disp),
    .ALUSrc(ALUSrc), .signextended(sign_extend));
  Multiplexer #(.width(16)) multiplexer_10 (
    .in0(Data_Mem_Addr), .in1(Data_Mem_Data), .out(multiplexer_10_out), .sel(MemtoReg));  // open: en
  or or_4 (nop, jal, jr, j, branch);
  Demultiplexer #(.width(16), .enable("false")) demultiplexer_1 (
    .out0(demultiplexer_1_out0), .out1(demultiplexer_1_out1), .in(rs), .sel(demultiplexer_3_out1[0]));
  Comparator #(.width(16)) comparator_1 (.a(multiplexer_8_out), .b(16'h2), .lt(comparator_1_lt));  // open: gt, eq
  Demultiplexer #(.enable("false")) demultiplexer_2 (
    .out0(demultiplexer_2_out0), .out1(demultiplexer_2_out1), .in(disp), .sel(demultiplexer_3_out1[0]));
  Demultiplexer #(.width(16), .enable("false")) demultiplexer_3 (
    .out1(demultiplexer_3_out1), .in(multiplexer_8_out), .sel(and_4_out));  // open: out0
  and and_4 (and_4_out, comparator_1_lt, disp);
  Register #(.width(16)) register_3 (
    .D(demultiplexer_1_out0), .en(demultiplexer_2_out0), .Q(Display_0), .clk(clk));  // open: clr
  Register #(.width(16)) register_4 (
    .D(demultiplexer_1_out1), .en(demultiplexer_2_out1), .Q(Display_1), .clk(clk));  // open: clr
  Hex_Digit_Display hex_digit_display_1 (.value(Display_0[11:8]));  // open: dp
  Hex_Digit_Display hex_digit_display_2 (.value(Display_0[15:12]));  // open: dp
  Hex_Digit_Display hex_digit_display_3 (.value(Display_1[15:12]));  // open: dp
  Hex_Digit_Display hex_digit_display_4 (.value(Display_1[11:8]));  // open: dp
  Hex_Digit_Display hex_digit_display_5 (.value(Display_0[3:0]));  // open: dp
  Hex_Digit_Display hex_digit_display_6 (.value(Display_0[7:4]));  // open: dp
  Hex_Digit_Display hex_digit_display_7 (.value(Display_1[7:4]));  // open: dp
  Hex_Digit_Display hex_digit_display_8 (.value(Display_1[3:0]));  // open: dp

  // Other names for the same wires on the sheet: Address[15:0] = Data_Mem_Addr; d0[15:0] = Display_0;
  //   d1[15:0] = Display_1; DataOut[15:0] = Data_Mem_Data; MemWrite = Data_Mem_Write

  // Notes on the sheet:
  //   This is the current PC that you need to send as OUTPUT
  //   This is the instruction that you would receive as INPUT
  //   This is a CLK that is an INPUT driven from the harness.
  //   Remember, this circuit is loaded from the harness to be tested!
  //   DO NOT CHANGE THE LOCATIONS OF THE INPUTS/OUTPUTS! IF YOU DO SO, YOU NEED TO MAKE SURE THE PINS ARE AT THE RIGHT PLACE!
  //   These are OUTPUTS to the circuit
  //   These are OUTPUTS to the circuit
endmodule

// alu
module ALU2 (
  input  [5:0] funct,
  input  [3:0] ALUOp,
  output [3:0] ALU_control_input
);

  Multiplexer #(.select(4), .width(4)) multiplexer_1 (
    .in0(funct[3:0]), .in1(4'b0110), .in2(4'b0111), .in3(4'b0000), .in4(4'b0001), .in5(4'b1000),
    .in6(4'b1001), .in7(4'b1010), .in8(4'b1011), .out(ALU_control_input), .sel(ALUOp));  // open: in9, in10, in11, in12, in13, in14, in15, en
endmodule

module control (
  input  [3:0] Con,
  output [3:0] ALUOp,
  output Registerd,
  output RegWrite,
  output jal,
  output j,
  output jr,
  output beq,
  output bne,
  output MemoryWrite,
  output MemorytoRegister,
  output disp,
  output ALUSrc,
  output signextended
);

  wire decoder_1_out1, decoder_1_out2, decoder_1_out3, decoder_1_out4, decoder_1_out5, decoder_1_out6,
       decoder_1_out13;

  Decoder #(.select(4), .enable("false")) decoder_1 (
    .out0(Registerd), .out1(decoder_1_out1), .out2(decoder_1_out2), .out3(decoder_1_out3),
    .out4(decoder_1_out4), .out5(decoder_1_out5), .out6(decoder_1_out6), .out7(jal), .out8(j), .out9(jr),
    .out10(beq), .out11(bne), .out12(MemoryWrite), .out13(decoder_1_out13), .out14(MemorytoRegister),
    .out15(disp), .sel(Con));
  or or_1 (signextended, decoder_1_out4, beq, bne, MemoryWrite, MemorytoRegister);
  Multiplexer #(.select(4), .width(4)) multiplexer_1 (
    .in0(4'b0000), .in1(4'b0110), .in2(4'b0111), .in3(4'b1000), .in4(4'b0001), .in5(4'b0011), .in6(4'b0100),
    .in10(4'b0010), .in11(4'b0010), .in12(4'b0001), .in13(4'b0101), .in14(4'b0001), .out(ALUOp), .sel(Con));  // open: in7, in8, in9, in15, en
  or or_2 (RegWrite, Registerd, decoder_1_out1, decoder_1_out2, decoder_1_out3, decoder_1_out4, decoder_1_out5, decoder_1_out6, jal, decoder_1_out13, MemorytoRegister);
  or or_3 (ALUSrc, MemorytoRegister, decoder_1_out13, decoder_1_out6, decoder_1_out5, decoder_1_out4, MemoryWrite);
endmodule
